# Fritzing sketch Moon_Light (saved by Fritzing 0.8.7b)
circuit board: 6.53811cm x 3.4cm
breadboards: 1

parts:
  R1 = Resistor [tolerance=±5% resistance=220 package=THT]
  R2 = Resistor [tolerance=±5% resistance=220 package=THT]
  R3 = Resistor [tolerance=±5% resistance=220 package=THT]
  LED = RGB LED (com. cathode, rgb) [package="5 mm [THT]"]
  S1 = Pushbutton [package="[THT]"]
  R4 = Resistor [tolerance=±5% resistance=220 package=THT]
  ATTINY84 = PICAXE-14M [part_number=ATtiny84 package=THT]
  J1 = female pin header, 2 pins [form="♀ (female)"]
  J2 = female pin header, 1 pin [form="♀ (female)"]
  J3 = female pin header, 1 pin [form="♀ (female)"]
  part = female pin header, 1 pin [form="♀ (female)"]  # not connected

nets:
  N1: R1.Pin_0, ATTINY84.In_0_/_ADC_0, J2.pin1
  N2: R1.Pin_1, LED.red_anode
  N3: R2.Pin_0, ATTINY84.In_1
  N4: R2.Pin_1, LED.green_anode
  N5: R3.Pin_0, ATTINY84.In_2
  N6: R3.Pin_1, LED.blue_anode
  N7: LED.common_cathode, R4.Pin_1, ATTINY84.0V
  N8: S1.Pin_1, S1.Pin_2, R4.Pin_0, ATTINY84.Out_3
  N9: S1.Pin_3, S1.Pin_4, ATTINY84.+V
  N10: ATTINY84.In_3_/_Infrain, J3.pin1
  N11: ATTINY84.Out_5, J1.pin2
  N12: ATTINY84.Out_4, J1.pin1

notes:
  fluuux.de
  +5V
  GND
  13
  10
  11
  12
  Moon
  light
  2012
